// Digital circuit part_c.dig as structural Verilog
module part_c (
  input  in_0,
  input  in_2,
  input  in_1,
  output out_0
);

  wire nfet_2_s, pfet_1_d, pfet_2_d, pfet_3_d;

  PFET pfet_1 (.G(in_2), .S(1'b1), .D(pfet_1_d));
  NFET nfet_1 (.G(in_2), .D(pfet_1_d), .S(1'b0));
  PFET pfet_2 (.G(in_0), .S(1'b1), .D(pfet_2_d));
  PFET pfet_3 (.G(pfet_1_d), .S(pfet_2_d), .D(pfet_3_d));
  NFET nfet_2 (.G(in_0), .D(pfet_3_d), .S(nfet_2_s));
  NFET nfet_3 (.G(in_1), .D(nfet_2_s), .S(1'b0));
  PFET pfet_4 (.G(in_1), .S(1'b1), .D(pfet_2_d));
  NFET nfet_4 (.G(pfet_1_d), .D(pfet_3_d), .S(1'b0));
  PFET pfet_5 (.G(pfet_3_d), .S(1'b1), .D(out_0));
  NFET nfet_5 (.G(pfet_3_d), .D(out_0), .S(1'b0));
endmodule

/* Test case part_c_test:
in_0 in_1 in_2 out_0
0 0 0 1
0 0 1 0
0 1 0 1
0 1 1 0
1 0 0 1
1 0 1 0
1 1 0 1
1 1 1 1
*/
